# Fritzing sketch ups_board (saved by Fritzing 0.8.3b)
breadboards: 1

parts:
  VCC1 = Battery
  D1 = Rectifier Diode [part_number=1N4007 package="300 mil [THT]"]
  D2 = Rectifier Diode [part_number=1N4007 package="300 mil [THT]"]
  D3 = Rectifier Diode [part_number=1N4007 package="300 mil [THT]"]
  D4 = Rectifier Diode [part_number=1N4007 package="300 mil [THT]"]
  R1 = Resistor [tolerance=±5% resistance=2.2k power=2W package=THT]
  D5 = Rectifier Diode [part_number=1N4001 package="300 mil [THT]"]
  D6 = Rectifier Diode [part_number=1N4001 package="300 mil [THT]"]
  U1 = Voltage Regulator - 5V [part_number=MC78T12 package="TO220 [THT]"]
  R2 = Resistor [tolerance=±5% resistance=220 package=THT]  # not connected
  12V_Li-Ion_Battery = Screw terminal - 2 pins [package=THT]
  R3 = Resistor [tolerance=±5% resistance=220 package=THT]
  J2_-_12V_DC_out = Screw terminal - 2 pins [package=THT]
  LED2 = LED - 5mm [color="Green (565nm)" package="5 mm [THT]"]
  R4 = Resistor [tolerance=±5% resistance=220 package=THT]
  LED3 = LED - 5mm [color="Red (633nm)" package="5 mm [THT]"]
  IC1 = IC, DIP package, 8 pins [chip_label=IC741]
  Q2 = NPN-Transistor [package="TO92 [THT]"]  # not connected
  Q3 = PNP-Transistor [package="TO92 [THT]"]

nets:
  N1: VCC1.-, D4.cathode, R3.Pin_1, J2_-_12V_DC_out.pin2, LED2.anode
  N2: VCC1.+, U1.input_voltage
  N3: D1.cathode, D4.anode
  N4: D1.anode, D3.cathode
  N5: D2.cathode, D3.anode
  N6: D2.anode, R1.Pin_0, U1.GND
  N7: R1.Pin_1, U1.output_voltage, Q3.E
  N8: D5.anode, D6.cathode, 12V_Li-Ion_Battery.pin1
  N9: R3.Pin_0, LED2.cathode
  N10: R4.Pin_0, LED3.anode
  N11: R4.Pin_1, IC1.pin6
