# Fritzing sketch ups (saved by Fritzing 0.8.3b)
breadboards: 1

parts:
  J1 = Screw terminal - 2 pins [package=THT]
  C1 = Ceramic Capacitor [capacitance=100nF package="100 mil [THT, multilayer]"]

nets:
  N1: J1.pin1, C1.1
  N2: J1.pin2, C1.0
